# Fritzing sketch Wiring Diagram (saved by Fritzing 0.6.3b)
breadboards: 1

parts:
  Arduino1 = Arduino
  Y_Servo = Basic Servo
  X_Servo = Basic Servo
  Laser = LED - 5mm [color="Red (633nm)" package="5 mm [THT]"]

nets:
  GND: Arduino1.GND, Y_Servo.gnd, X_Servo.gnd, Laser.anode
  N1: Arduino1.D12, Laser.cathode
  N2: Arduino1.D6, Y_Servo.pulse
  VCC: Arduino1.+5V, Y_Servo.vcc, X_Servo.vcc
